# Fritzing sketch Reverse Geocache (saved by Fritzing 0.9.3b)
breadboards: 1

parts:
  BUTTON1 = Waterproof Pushbutton (green)
  Part1 = Arduino Uno (Rev3)
  BAT1 = BC9VPC [package=bc9vpc]
  Part2 = Adafruit Ultimate GPS v3 [part_number="Adafruit #746"]
  U2 = LCD-16X2 [package=lcd-16x2]
  J1 = Basic Servo
  R1 = Resistor [tolerance=±5% resistance=220 package=THT]
  POT1 = Breadboard Trimpot

nets:
  N1: BUTTON1.no_name_yet#1, Part1.VIN
  N2: BUTTON1.no_name_yet#2, BAT1.V+
  N3: BUTTON1.no_name_yet#4, Part1.D10_PWM/SS
  GND: BUTTON1.no_name_yet#5, Part1.GND, BAT1.V-, Part2.GND, U2.VSS, U2.R_W, U2.K, J1.gnd, POT1.PIN3
  N4: Part1.D9_PWM, J1.pulse
  N5: Part1.D11_PWM/MOSI, U2.E
  N6: Part1.D12/MISO, U2.RS
  N7: Part1.D2, Part2.RX
  N8: Part1.D3_PWM, Part2.TX
  N9: Part1.D4, U2.DB7
  N10: Part1.D5_PWM, U2.DB6
  N11: Part1.D6_PWM, U2.DB5
  N12: Part1.D7, U2.DB4
  5V: Part1.5V, Part2.VIN, U2.VDD, J1.vcc, R1.Pin_0, POT1.PIN1
  N13: U2.VO, POT1.PIN2
  N14: U2.A, R1.Pin_1

custom parts:
  Waterproof Pushbutton (green): Waterproof Illuminated Pushbutton (green)
  Adafruit Ultimate GPS v3: We carry a few different GPS modules here in the Adafruit shop, but none that satisfied our every desire - that's why we designed this little GPS breakout board. We believe this is the Ultimate GPS module, so we named it that. It's got everything you want and more: -165 dBm sensitivity, 10 Hz updates, 66 channels 5V friendly design and only 20mA current draw Breadboard friendly + two mounting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
